// Logisim project Reloj.circ as structural Verilog: 1 circuit, main circuit main
module main (
);

  wire and_1_out, and_2_out, and_3_out, and_4_out, and_5_out, and_7_out, and_8_out, and_9_out, and_10_out,
       clock_1_out, j_k_ff_8_qn, j_k_ff_9_qn, j_k_ff_10_qn, j_k_ff_11_qn, n7seg_encoder_1_a,
       n7seg_encoder_1_b, n7seg_encoder_1_c, n7seg_encoder_1_d, n7seg_encoder_1_e, n7seg_encoder_1_f,
       n7seg_encoder_1_g, n7seg_encoder_2_a, n7seg_encoder_2_b, n7seg_encoder_2_c, n7seg_encoder_2_d,
       n7seg_encoder_2_e, n7seg_encoder_2_f, n7seg_encoder_2_g, n7seg_encoder_3_a, n7seg_encoder_3_b,
       n7seg_encoder_3_c, n7seg_encoder_3_d, n7seg_encoder_3_e, n7seg_encoder_3_f, n7seg_encoder_3_g,
       n7seg_encoder_4_a, n7seg_encoder_4_b, n7seg_encoder_4_c, n7seg_encoder_4_d, n7seg_encoder_4_e,
       n7seg_encoder_4_f, n7seg_encoder_4_g, or_1_out;
  wire [0:0] and_6_out;
  wire [2:0] j_k_ff_5_q;
  wire [3:0] adder_1_out, j_k_ff_1_q, j_k_ff_8_q;

  Clock clock_1 (.out(clock_1_out));
  J_K_Flip_Flop j_k_ff_1 (
    .J(1'b1), .clk(clock_1_out), .K(1'b1), .Q(j_k_ff_1_q[0]), .en(1'b1), .reset(and_3_out));  // open: Qn, preset
  and and_1 (and_1_out, j_k_ff_1_q[0], j_k_ff_1_q[1]);
  J_K_Flip_Flop j_k_ff_2 (
    .J(j_k_ff_1_q[0]), .clk(clock_1_out), .K(j_k_ff_1_q[0]), .Q(j_k_ff_1_q[1]), .en(1'b1), .reset(and_3_out));  // open: Qn, preset
  J_K_Flip_Flop j_k_ff_3 (
    .J(and_1_out), .clk(clock_1_out), .K(and_1_out), .Q(j_k_ff_1_q[2]), .en(1'b1), .reset(and_3_out));  // open: Qn, preset
  and and_2 (and_2_out, and_1_out, j_k_ff_1_q[2]);
  and and_3 (and_3_out, j_k_ff_1_q[1], j_k_ff_1_q[3]);
  J_K_Flip_Flop j_k_ff_4 (
    .J(and_2_out), .clk(clock_1_out), .K(and_2_out), .Q(j_k_ff_1_q[3]), .en(1'b1), .reset(and_3_out));  // open: Qn, preset
  _7_Segment_Display u_7_segment_display_1 (
    .g(n7seg_encoder_1_g), .f(n7seg_encoder_1_f), .a(n7seg_encoder_1_a), .b(n7seg_encoder_1_b),
    .e(n7seg_encoder_1_e), .d(n7seg_encoder_1_d), .c(n7seg_encoder_1_c));  // open: dp
  _7seg_encoder u_7seg_encoder_1 (
    .Input({1'b0, j_k_ff_5_q}), .E(n7seg_encoder_1_e), .D(n7seg_encoder_1_d), .C(n7seg_encoder_1_c),
    .G(n7seg_encoder_1_g), .F(n7seg_encoder_1_f), .A(n7seg_encoder_1_a), .B(n7seg_encoder_1_b));
  J_K_Flip_Flop j_k_ff_5 (
    .J(1'b1), .clk(and_3_out), .K(1'b1), .Q(j_k_ff_5_q[0]), .en(1'b1), .reset(and_5_out));  // open: Qn, preset
  _7_Segment_Display u_7_segment_display_2 (
    .g(n7seg_encoder_2_g), .f(n7seg_encoder_2_f), .a(n7seg_encoder_2_a), .b(n7seg_encoder_2_b),
    .e(n7seg_encoder_2_e), .d(n7seg_encoder_2_d), .c(n7seg_encoder_2_c));  // open: dp
  _7seg_encoder u_7seg_encoder_2 (
    .Input(j_k_ff_1_q), .E(n7seg_encoder_2_e), .D(n7seg_encoder_2_d), .C(n7seg_encoder_2_c),
    .G(n7seg_encoder_2_g), .F(n7seg_encoder_2_f), .A(n7seg_encoder_2_a), .B(n7seg_encoder_2_b));
  J_K_Flip_Flop j_k_ff_6 (
    .J(j_k_ff_5_q[0]), .clk(and_3_out), .K(j_k_ff_5_q[0]), .Q(j_k_ff_5_q[1]), .en(1'b1), .reset(and_5_out));  // open: Qn, preset
  and and_4 (and_4_out, j_k_ff_5_q[0], j_k_ff_5_q[1]);
  J_K_Flip_Flop j_k_ff_7 (
    .J(and_4_out), .clk(and_3_out), .K(and_4_out), .Q(j_k_ff_5_q[2]), .en(1'b1), .reset(and_5_out));  // open: Qn, preset
  Adder #(.width(4)) adder_1 (
    .a(j_k_ff_8_q), .b({1'b0, {2{and_6_out[0]}}, 1'b0}), .out(adder_1_out));  // open: cin, cout
  and and_5 (and_5_out, j_k_ff_5_q[1], j_k_ff_5_q[2]);
  or or_1 (or_1_out, j_k_ff_8_q[1], j_k_ff_8_q[2]);
  and and_6 (and_6_out[0], or_1_out, j_k_ff_8_q[3]);
  J_K_Flip_Flop j_k_ff_8 (
    .J(1'b1), .clk(and_5_out), .K(1'b1), .Q(j_k_ff_8_q[0]), .Qn(j_k_ff_8_qn), .preset(and_8_out), .en(1'b1),
    .reset(and_10_out));
  and and_7 (and_7_out, j_k_ff_8_q[0], j_k_ff_8_q[1]);
  J_K_Flip_Flop j_k_ff_9 (
    .J(j_k_ff_8_q[0]), .clk(and_5_out), .K(j_k_ff_8_q[0]), .Q(j_k_ff_8_q[1]), .Qn(j_k_ff_9_qn), .en(1'b1),
    .reset(and_10_out));  // open: preset
  and and_8 (and_8_out, j_k_ff_8_qn, j_k_ff_9_qn, j_k_ff_10_qn, j_k_ff_11_qn);
  J_K_Flip_Flop j_k_ff_10 (
    .J(and_7_out), .clk(and_5_out), .K(and_7_out), .Q(j_k_ff_8_q[2]), .Qn(j_k_ff_10_qn), .reset(and_10_out));  // open: preset, en
  and and_9 (and_9_out, and_7_out, j_k_ff_8_q[2]);
  _7_Segment_Display u_7_segment_display_3 (
    .g(n7seg_encoder_3_g), .f(n7seg_encoder_3_f), .a(n7seg_encoder_3_a), .b(n7seg_encoder_3_b),
    .e(n7seg_encoder_3_e), .d(n7seg_encoder_3_d), .c(n7seg_encoder_3_c));  // open: dp
  _7seg_encoder u_7seg_encoder_3 (
    .Input({3'b000, and_6_out[0]}), .E(n7seg_encoder_3_e), .D(n7seg_encoder_3_d), .C(n7seg_encoder_3_c),
    .G(n7seg_encoder_3_g), .F(n7seg_encoder_3_f), .A(n7seg_encoder_3_a), .B(n7seg_encoder_3_b));
  J_K_Flip_Flop j_k_ff_11 (
    .J(and_9_out), .clk(and_5_out), .K(and_9_out), .Q(j_k_ff_8_q[3]), .Qn(j_k_ff_11_qn), .en(1'b1),
    .reset(and_10_out));  // open: preset
  _7_Segment_Display u_7_segment_display_4 (
    .g(n7seg_encoder_4_g), .f(n7seg_encoder_4_f), .a(n7seg_encoder_4_a), .b(n7seg_encoder_4_b),
    .e(n7seg_encoder_4_e), .d(n7seg_encoder_4_d), .c(n7seg_encoder_4_c));  // open: dp
  _7seg_encoder u_7seg_encoder_4 (
    .Input(adder_1_out), .E(n7seg_encoder_4_e), .D(n7seg_encoder_4_d), .C(n7seg_encoder_4_c),
    .G(n7seg_encoder_4_g), .F(n7seg_encoder_4_f), .A(n7seg_encoder_4_a), .B(n7seg_encoder_4_b));
  and and_10 (and_10_out, j_k_ff_8_q[2], j_k_ff_8_q[0], j_k_ff_8_q[3]);

  // Notes on the sheet:
  //   Minutos
  //   Horas
endmodule
