// Logisim project display.circ as structural Verilog: 4 circuits, main circuit DDA
module DDA (
  input  LSB,
  input  in_2,
  input  in_3,
  input  MSB,
  output LSB_2,
  output out_6,
  output out_7,
  output MSB_2
);

  wire decoder_1_out0, decoder_1_out1, decoder_1_out2, decoder_1_out3, decoder_1_out4, decoder_1_out5,
       decoder_1_out6, decoder_1_out7, decoder_1_out8, nor_1_out, or_1_out, or_2_out;
  wire [3:0] adder_1_out, multiplexer_1_out, pull_resistor_2_node;
  wire [3:3] pull_resistor_1_node;

  Pull_Resistor pull_resistor_1 (.node(pull_resistor_1_node[3]));
  or or_1 (or_1_out, decoder_1_out0, decoder_1_out1, decoder_1_out2, decoder_1_out3, decoder_1_out4);
  Decoder #(.select(4), .disabled(0), .enable("false")) decoder_1 (
    .out0(decoder_1_out0), .out1(decoder_1_out1), .out2(decoder_1_out2), .out3(decoder_1_out3),
    .out4(decoder_1_out4), .out5(decoder_1_out5), .out6(decoder_1_out6), .out7(decoder_1_out7),
    .out8(decoder_1_out8), .sel({MSB, in_3, in_2, LSB}));  // open: out9, out10, out11, out12, out13, out14, out15
  nor nor_1 (nor_1_out, or_2_out, or_1_out);
  Multiplexer #(.width(4)) multiplexer_1 (
    .in0({MSB, in_3, in_2, LSB}), .in1(adder_1_out), .out(multiplexer_1_out), .sel(or_2_out));  // open: en
  Adder #(.width(4)) adder_1 (
    .a({MSB, in_3, in_2, LSB}), .b({{2{pull_resistor_1_node[3]}}, 2'b11}), .out(adder_1_out));  // open: cin, cout
  Pull_Resistor pull_resistor_2 (.node(pull_resistor_2_node));
  or or_2 (or_2_out, decoder_1_out5, decoder_1_out6, decoder_1_out7, decoder_1_out8);
  Multiplexer #(.width(4)) multiplexer_2 (
    .in0(multiplexer_1_out), .in1(pull_resistor_2_node), .out({MSB_2, out_7, out_6, LSB_2}), .sel(nor_1_out));  // open: en
endmodule

module _8_Bit_DDA (
  input  [7:0] in_1,
  output [3:0] out_2,
  output [3:0] out_3,
  output [3:0] out_4
);

  wire dda_1_lsb_2, dda_1_msb_2, dda_1_out_6, dda_1_out_7, dda_2_lsb_2, dda_2_msb_2, dda_2_out_6,
       dda_2_out_7, dda_3_lsb_2, dda_3_msb_2, dda_3_out_6, dda_3_out_7, dda_4_lsb_2, dda_4_msb_2,
       dda_4_out_6, dda_4_out_7, dda_5_lsb_2, dda_5_msb_2, dda_5_out_6, dda_5_out_7, dda_6_lsb_2,
       dda_6_out_6, dda_6_out_7, dda_7_lsb_2, dda_7_msb_2, dda_7_out_6, dda_7_out_7, dda_8_lsb_2,
       dda_8_msb_2, dda_8_out_6, dda_8_out_7, dda_9_lsb_2, dda_9_out_6, dda_9_out_7, dda_10_lsb_2,
       dda_10_out_6, dda_10_out_7, pull_resistor_1_node;

  DDA dda_1 (
    .LSB(pull_resistor_1_node), .in_2(pull_resistor_1_node), .in_3(pull_resistor_1_node),
    .MSB(pull_resistor_1_node), .LSB_2(dda_1_lsb_2), .out_6(dda_1_out_6), .out_7(dda_1_out_7),
    .MSB_2(dda_1_msb_2));
  Pull_Resistor pull_resistor_1 (.node(pull_resistor_1_node));
  DDA dda_2 (
    .LSB(in_1[6]), .in_2(dda_3_lsb_2), .in_3(dda_3_out_6), .MSB(dda_3_out_7), .LSB_2(dda_2_lsb_2),
    .out_6(dda_2_out_6), .out_7(dda_2_out_7), .MSB_2(dda_2_msb_2));
  DDA dda_3 (
    .LSB(in_1[7]), .in_2(dda_1_lsb_2), .in_3(dda_1_out_6), .MSB(dda_1_out_7), .LSB_2(dda_3_lsb_2),
    .out_6(dda_3_out_6), .out_7(dda_3_out_7), .MSB_2(dda_3_msb_2));
  DDA dda_4 (
    .LSB(in_1[4]), .in_2(dda_5_lsb_2), .in_3(dda_5_out_6), .MSB(dda_5_out_7), .LSB_2(dda_4_lsb_2),
    .out_6(dda_4_out_6), .out_7(dda_4_out_7), .MSB_2(dda_4_msb_2));
  DDA dda_5 (
    .LSB(in_1[5]), .in_2(dda_2_lsb_2), .in_3(dda_2_out_6), .MSB(dda_2_out_7), .LSB_2(dda_5_lsb_2),
    .out_6(dda_5_out_6), .out_7(dda_5_out_7), .MSB_2(dda_5_msb_2));
  DDA dda_6 (
    .LSB(dda_5_msb_2), .in_2(dda_2_msb_2), .in_3(dda_3_msb_2), .MSB(dda_1_msb_2), .LSB_2(dda_6_lsb_2),
    .out_6(dda_6_out_6), .out_7(dda_6_out_7), .MSB_2(out_4[3]));
  DDA dda_7 (
    .LSB(in_1[2]), .in_2(dda_8_lsb_2), .in_3(dda_8_out_6), .MSB(dda_8_out_7), .LSB_2(dda_7_lsb_2),
    .out_6(dda_7_out_6), .out_7(dda_7_out_7), .MSB_2(dda_7_msb_2));
  DDA dda_8 (
    .LSB(in_1[3]), .in_2(dda_4_lsb_2), .in_3(dda_4_out_6), .MSB(dda_4_out_7), .LSB_2(dda_8_lsb_2),
    .out_6(dda_8_out_6), .out_7(dda_8_out_7), .MSB_2(dda_8_msb_2));
  DDA dda_9 (
    .LSB(dda_8_msb_2), .in_2(dda_10_lsb_2), .in_3(dda_10_out_6), .MSB(dda_10_out_7), .LSB_2(dda_9_lsb_2),
    .out_6(dda_9_out_6), .out_7(dda_9_out_7), .MSB_2(out_4[1]));
  DDA dda_10 (
    .LSB(dda_4_msb_2), .in_2(dda_6_lsb_2), .in_3(dda_6_out_6), .MSB(dda_6_out_7), .LSB_2(dda_10_lsb_2),
    .out_6(dda_10_out_6), .out_7(dda_10_out_7), .MSB_2(out_4[2]));
  DDA dda_11 (
    .LSB(in_1[1]), .in_2(dda_7_lsb_2), .in_3(dda_7_out_6), .MSB(dda_7_out_7), .LSB_2(out_2[1]),
    .out_6(out_2[2]), .out_7(out_2[3]), .MSB_2(out_3[0]));
  DDA dda_12 (
    .LSB(dda_7_msb_2), .in_2(dda_9_lsb_2), .in_3(dda_9_out_6), .MSB(dda_9_out_7), .LSB_2(out_3[1]),
    .out_6(out_3[2]), .out_7(out_3[3]), .MSB_2(out_4[0]));

  assign out_2[0] = in_1[0];
endmodule

module _7seg_encoder (
  input  [3:0] Input,
  output G,
  output F,
  output A,
  output B,
  output E,
  output D,
  output C
);

  wire decoder_1_out0, decoder_1_out1, decoder_1_out2, decoder_1_out3, decoder_1_out4, decoder_1_out5,
       decoder_1_out6, decoder_1_out7, decoder_1_out8, decoder_1_out9;

  Decoder #(.select(4), .enable("false")) decoder_1 (
    .out0(decoder_1_out0), .out1(decoder_1_out1), .out2(decoder_1_out2), .out3(decoder_1_out3),
    .out4(decoder_1_out4), .out5(decoder_1_out5), .out6(decoder_1_out6), .out7(decoder_1_out7),
    .out8(decoder_1_out8), .out9(decoder_1_out9), .sel(Input));  // open: out10, out11, out12, out13, out14, out15
  or u_A (A, decoder_1_out0, decoder_1_out2, decoder_1_out3, decoder_1_out5, decoder_1_out6, decoder_1_out7, decoder_1_out8, decoder_1_out9);
  or u_B (B, decoder_1_out0, decoder_1_out1, decoder_1_out3, decoder_1_out4, decoder_1_out7, decoder_1_out8, decoder_1_out9, decoder_1_out2);
  or u_C (C, decoder_1_out0, decoder_1_out1, decoder_1_out3, decoder_1_out4, decoder_1_out5, decoder_1_out6, decoder_1_out7, decoder_1_out8, decoder_1_out9);
  _7_Segment_Display u_7_segment_display_1 (.g(G), .f(F), .a(A), .b(B), .e(E), .d(D), .c(C));  // open: dp
  or u_D (D, decoder_1_out0, decoder_1_out2, decoder_1_out3, decoder_1_out5, decoder_1_out6, decoder_1_out8);
  or u_E (E, decoder_1_out0, decoder_1_out6, decoder_1_out8, decoder_1_out2);
  or u_F (F, decoder_1_out0, decoder_1_out4, decoder_1_out5, decoder_1_out6, decoder_1_out7, decoder_1_out8, decoder_1_out9);
  or u_G (G, decoder_1_out2, decoder_1_out3, decoder_1_out4, decoder_1_out5, decoder_1_out6, decoder_1_out8, decoder_1_out9);
endmodule

module display (
  input  [7:0] in_1
);

  wire n7seg_encoder_1_a, n7seg_encoder_1_b, n7seg_encoder_1_c, n7seg_encoder_1_d, n7seg_encoder_1_e,
       n7seg_encoder_1_f, n7seg_encoder_1_g, n7seg_encoder_2_a, n7seg_encoder_2_b, n7seg_encoder_2_c,
       n7seg_encoder_2_d, n7seg_encoder_2_e, n7seg_encoder_2_f, n7seg_encoder_2_g, n7seg_encoder_3_a,
       n7seg_encoder_3_b, n7seg_encoder_3_c, n7seg_encoder_3_d, n7seg_encoder_3_e, n7seg_encoder_3_f,
       n7seg_encoder_3_g;
  wire [3:0] n8_bit_dda_1_out_2, n8_bit_dda_1_out_3, n8_bit_dda_1_out_4;

  _8_Bit_DDA u_8_bit_dda_1 (
    .in_1(in_1), .out_2(n8_bit_dda_1_out_2), .out_3(n8_bit_dda_1_out_3), .out_4(n8_bit_dda_1_out_4));
  _7_Segment_Display u_7_segment_display_1 (
    .g(n7seg_encoder_1_g), .f(n7seg_encoder_1_f), .a(n7seg_encoder_1_a), .b(n7seg_encoder_1_b),
    .e(n7seg_encoder_1_e), .d(n7seg_encoder_1_d), .c(n7seg_encoder_1_c));  // open: dp
  _7seg_encoder u_7seg_encoder_1 (
    .Input(n8_bit_dda_1_out_4), .E(n7seg_encoder_1_e), .D(n7seg_encoder_1_d), .C(n7seg_encoder_1_c),
    .G(n7seg_encoder_1_g), .F(n7seg_encoder_1_f), .A(n7seg_encoder_1_a), .B(n7seg_encoder_1_b));
  _7_Segment_Display u_7_segment_display_2 (
    .g(n7seg_encoder_2_g), .f(n7seg_encoder_2_f), .a(n7seg_encoder_2_a), .b(n7seg_encoder_2_b),
    .e(n7seg_encoder_2_e), .d(n7seg_encoder_2_d), .c(n7seg_encoder_2_c));  // open: dp
  _7seg_encoder u_7seg_encoder_2 (
    .Input(n8_bit_dda_1_out_3), .E(n7seg_encoder_2_e), .D(n7seg_encoder_2_d), .C(n7seg_encoder_2_c),
    .G(n7seg_encoder_2_g), .F(n7seg_encoder_2_f), .A(n7seg_encoder_2_a), .B(n7seg_encoder_2_b));
  _7_Segment_Display u_7_segment_display_3 (
    .g(n7seg_encoder_3_g), .f(n7seg_encoder_3_f), .a(n7seg_encoder_3_a), .b(n7seg_encoder_3_b),
    .e(n7seg_encoder_3_e), .d(n7seg_encoder_3_d), .c(n7seg_encoder_3_c));  // open: dp
  _7seg_encoder u_7seg_encoder_3 (
    .Input(n8_bit_dda_1_out_2), .E(n7seg_encoder_3_e), .D(n7seg_encoder_3_d), .C(n7seg_encoder_3_c),
    .G(n7seg_encoder_3_g), .F(n7seg_encoder_3_f), .A(n7seg_encoder_3_a), .B(n7seg_encoder_3_b));
endmodule
